# Fritzing sketch puppy_electronics (saved by Fritzing 0.9.2b)

parts:
  Part1 = Arduino Mega 2560 (Rev3)
  Part2 = IMU Digital Combo Board 6DOF
  Part3 = NCP1400 Step-Up Breakout
  J1 = Basic Servo
  J2 = Basic Servo
  J3 = Basic Servo
  J4 = Basic Servo
  Power_plug1 = Power plug

nets:
  N1: Part1.D21/SCL, Part2.SDA
  N2: Part1.D20/SDA, Part2.SCL
  N3: Part1.D10_PWM, J4.pulse
  N4: Part1.D9_PWM, J3.pulse
  3V3: Part1.3V3, Part2.3.3V
  GND: Part1.GND, Part2.GND
  N5: Part1.D2_PWM, Part2.INT0
  N6: Part1.D6_PWM, J1.pulse
  N7: Part1.D7_PWM, J2.pulse
  GND_2: Part3.GND, J1.gnd, J2.gnd, J3.gnd, J4.gnd, Power_plug1.GND
  VCC: Part3.VOUT, J1.vcc, J2.vcc, J3.vcc, J4.vcc
  VIN: Part3.VIN, Power_plug1.VCC
